# Fritzing sketch Buitenverlichting sensor board v1.3 (saved by Fritzing 0.9.2b)
circuit board: 10cm x 21cm
breadboards: 1

parts:
  LED1 = LEDs [package=led10mm]
  Light_sensor = Ambient Light Sensor (TEMT6000 Breakout Board)
  R1 = Resistor [tolerance=±5% resistance=220 package=THT]
  Relay = Keyes Relay [package=THT]
  RTC_Module_(Clock) = Real Time Clock Module - DS1307 RTC Breakout Board
  Power_plug1 = Power plug
  Arduino_Uno = Arduino Uno (Rev3)
  V1 = DC Power [voltage=5]  # not connected
  Relay1 = male pin header, 3 pins [form="♂ (male)"]

nets:
  N1: LED1.A, Arduino_Uno.D8
  N2: LED1.C, R1.Pin_0
  5V: Light_sensor.VCC, RTC_Module_(Clock).5V, Arduino_Uno.5V, Relay1.pin2
  GND: Light_sensor.GND, R1.Pin_1, RTC_Module_(Clock).GND, Arduino_Uno.GND, Relay1.pin3
  N3: Light_sensor.S, Arduino_Uno.A0
  N4: Relay.C, Power_plug1.VCC
  N5: RTC_Module_(Clock).SCL, Arduino_Uno.A5/SCL
  N6: RTC_Module_(Clock).SDA, Arduino_Uno.A4/SDA
  N7: Arduino_Uno.D9_PWM, Relay1.pin1

notes:
  220 V
  GND
  Lights on 220 V

custom parts:
  Keyes Relay: The Keyes 5V relay module is suitable for SCM development, home appliance control. It uses a 5V~12V TIL control signal which can control DC / AC signal.
